// Logisim project TRABALHO.circ as structural Verilog
module Registrador (
  input  [31:0] a,
  input  W_En,
  input  CLK,
  output [31:0] s
);

  wire multiplexer_1_out, multiplexer_2_out, multiplexer_3_out, multiplexer_4_out, multiplexer_5_out,
       multiplexer_6_out, multiplexer_7_out, multiplexer_8_out, multiplexer_9_out, multiplexer_10_out,
       multiplexer_11_out, multiplexer_12_out, multiplexer_13_out, multiplexer_14_out, multiplexer_15_out,
       multiplexer_16_out, multiplexer_17_out, multiplexer_18_out, multiplexer_19_out, multiplexer_20_out,
       multiplexer_21_out, multiplexer_22_out, multiplexer_23_out, multiplexer_24_out, multiplexer_25_out,
       multiplexer_26_out, multiplexer_27_out, multiplexer_28_out, multiplexer_29_out, multiplexer_30_out,
       multiplexer_31_out, multiplexer_32_out;

  Multiplexer multiplexer_1 (.in0(s[0]), .in1(a[0]), .out(multiplexer_1_out), .sel(W_En));
  Multiplexer multiplexer_2 (.in0(s[1]), .in1(a[1]), .out(multiplexer_2_out), .sel(W_En));
  Multiplexer multiplexer_3 (.in0(s[2]), .in1(a[2]), .out(multiplexer_3_out), .sel(W_En));
  Multiplexer multiplexer_4 (.in0(s[3]), .in1(a[3]), .out(multiplexer_4_out), .sel(W_En));
  Multiplexer multiplexer_5 (.in0(s[4]), .in1(a[4]), .out(multiplexer_5_out), .sel(W_En));
  Multiplexer multiplexer_6 (.in0(s[5]), .in1(a[5]), .out(multiplexer_6_out), .sel(W_En));
  Multiplexer multiplexer_7 (.in0(s[6]), .in1(a[6]), .out(multiplexer_7_out), .sel(W_En));
  Multiplexer multiplexer_8 (.in0(s[7]), .in1(a[7]), .out(multiplexer_8_out), .sel(W_En));
  Multiplexer multiplexer_9 (.in0(s[8]), .in1(a[8]), .out(multiplexer_9_out), .sel(W_En));
  Multiplexer multiplexer_10 (.in0(s[9]), .in1(a[9]), .out(multiplexer_10_out), .sel(W_En));
  Multiplexer multiplexer_11 (.in0(s[10]), .in1(a[10]), .out(multiplexer_11_out), .sel(W_En));
  Multiplexer multiplexer_12 (.in0(s[11]), .in1(a[11]), .out(multiplexer_12_out), .sel(W_En));
  Multiplexer multiplexer_13 (.in0(s[12]), .in1(a[12]), .out(multiplexer_13_out), .sel(W_En));
  Multiplexer multiplexer_14 (.in0(s[13]), .in1(a[13]), .out(multiplexer_14_out), .sel(W_En));
  Multiplexer multiplexer_15 (.in0(s[14]), .in1(a[14]), .out(multiplexer_15_out), .sel(W_En));
  Multiplexer multiplexer_16 (.in0(s[15]), .in1(a[15]), .out(multiplexer_16_out), .sel(W_En));
  Multiplexer multiplexer_17 (.in0(s[16]), .in1(a[16]), .out(multiplexer_17_out), .sel(W_En));
  Multiplexer multiplexer_18 (.in0(s[17]), .in1(a[17]), .out(multiplexer_18_out), .sel(W_En));
  Multiplexer multiplexer_19 (.in0(s[18]), .in1(a[18]), .out(multiplexer_19_out), .sel(W_En));
  Multiplexer multiplexer_20 (.in0(s[19]), .in1(a[19]), .out(multiplexer_20_out), .sel(W_En));
  Multiplexer multiplexer_21 (.in0(s[20]), .in1(a[20]), .out(multiplexer_21_out), .sel(W_En));
  Multiplexer multiplexer_22 (.in0(s[21]), .in1(a[21]), .out(multiplexer_22_out), .sel(W_En));
  Multiplexer multiplexer_23 (.in0(s[22]), .in1(a[22]), .out(multiplexer_23_out), .sel(W_En));
  Multiplexer multiplexer_24 (.in0(s[23]), .in1(a[23]), .out(multiplexer_24_out), .sel(W_En));
  Multiplexer multiplexer_25 (.in0(s[24]), .in1(a[24]), .out(multiplexer_25_out), .sel(W_En));
  Multiplexer multiplexer_26 (.in0(s[25]), .in1(a[25]), .out(multiplexer_26_out), .sel(W_En));
  Multiplexer multiplexer_27 (.in0(s[26]), .in1(a[26]), .out(multiplexer_27_out), .sel(W_En));
  Multiplexer multiplexer_28 (.in0(s[27]), .in1(a[27]), .out(multiplexer_28_out), .sel(W_En));
  Multiplexer multiplexer_29 (.in0(s[28]), .in1(a[28]), .out(multiplexer_29_out), .sel(W_En));
  Multiplexer multiplexer_30 (.in0(s[29]), .in1(a[29]), .out(multiplexer_30_out), .sel(W_En));
  Multiplexer multiplexer_31 (.in0(s[30]), .in1(a[30]), .out(multiplexer_31_out), .sel(W_En));
  Multiplexer multiplexer_32 (.in0(s[31]), .in1(a[31]), .out(multiplexer_32_out), .sel(W_En));
  D_Flip_Flop d_ff_1 (.D(multiplexer_1_out), .clk(CLK), .Q(s[0]));  // open: Qn, preset, reset
  D_Flip_Flop d_ff_2 (.D(multiplexer_2_out), .clk(CLK), .Q(s[1]));  // open: Qn, preset, reset
  D_Flip_Flop d_ff_3 (.D(multiplexer_3_out), .clk(CLK), .Q(s[2]));  // open: Qn, preset, reset
  D_Flip_Flop d_ff_4 (.D(multiplexer_4_out), .clk(CLK), .Q(s[3]));  // open: Qn, preset, reset
  D_Flip_Flop d_ff_5 (.D(multiplexer_5_out), .clk(CLK), .Q(s[4]));  // open: Qn, preset, reset
  D_Flip_Flop d_ff_6 (.D(multiplexer_6_out), .clk(CLK), .Q(s[5]));  // open: Qn, preset, reset
  D_Flip_Flop d_ff_7 (.D(multiplexer_7_out), .clk(CLK), .Q(s[6]));  // open: Qn, preset, reset
  D_Flip_Flop d_ff_8 (.D(multiplexer_8_out), .clk(CLK), .Q(s[7]));  // open: Qn, preset, reset
  D_Flip_Flop d_ff_9 (.D(multiplexer_9_out), .clk(CLK), .Q(s[8]));  // open: Qn, preset, reset
  D_Flip_Flop d_ff_10 (.D(multiplexer_10_out), .clk(CLK), .Q(s[9]));  // open: Qn, preset, reset
  D_Flip_Flop d_ff_11 (.D(multiplexer_11_out), .clk(CLK), .Q(s[10]));  // open: Qn, preset, reset
  D_Flip_Flop d_ff_12 (.D(multiplexer_12_out), .clk(CLK), .Q(s[11]));  // open: Qn, preset, reset
  D_Flip_Flop d_ff_13 (.D(multiplexer_13_out), .clk(CLK), .Q(s[12]));  // open: Qn, preset, reset
  D_Flip_Flop d_ff_14 (.D(multiplexer_14_out), .clk(CLK), .Q(s[13]));  // open: Qn, preset, reset
  D_Flip_Flop d_ff_15 (.D(multiplexer_15_out), .clk(CLK), .Q(s[14]));  // open: Qn, preset, reset
  D_Flip_Flop d_ff_16 (.D(multiplexer_16_out), .clk(CLK), .Q(s[15]));  // open: Qn, preset, reset
  D_Flip_Flop d_ff_17 (.D(multiplexer_17_out), .clk(CLK), .Q(s[16]));  // open: Qn, preset, reset
  D_Flip_Flop d_ff_18 (.D(multiplexer_18_out), .clk(CLK), .Q(s[17]));  // open: Qn, preset, reset
  D_Flip_Flop d_ff_19 (.D(multiplexer_19_out), .clk(CLK), .Q(s[18]));  // open: Qn, preset, reset
  D_Flip_Flop d_ff_20 (.D(multiplexer_20_out), .clk(CLK), .Q(s[19]));  // open: Qn, preset, reset
  D_Flip_Flop d_ff_21 (.D(multiplexer_21_out), .clk(CLK), .Q(s[20]));  // open: Qn, preset, reset
  D_Flip_Flop d_ff_22 (.D(multiplexer_22_out), .clk(CLK), .Q(s[21]));  // open: Qn, preset, reset
  D_Flip_Flop d_ff_23 (.D(multiplexer_23_out), .clk(CLK), .Q(s[22]));  // open: Qn, preset, reset
  D_Flip_Flop d_ff_24 (.D(multiplexer_24_out), .clk(CLK), .Q(s[23]));  // open: Qn, preset, reset
  D_Flip_Flop d_ff_25 (.D(multiplexer_25_out), .clk(CLK), .Q(s[24]));  // open: Qn, preset, reset
  D_Flip_Flop d_ff_26 (.D(multiplexer_26_out), .clk(CLK), .Q(s[25]));  // open: Qn, preset, reset
  D_Flip_Flop d_ff_27 (.D(multiplexer_27_out), .clk(CLK), .Q(s[26]));  // open: Qn, preset, reset
  D_Flip_Flop d_ff_28 (.D(multiplexer_28_out), .clk(CLK), .Q(s[27]));  // open: Qn, preset, reset
  D_Flip_Flop d_ff_29 (.D(multiplexer_29_out), .clk(CLK), .Q(s[28]));  // open: Qn, preset, reset
  D_Flip_Flop d_ff_30 (.D(multiplexer_30_out), .clk(CLK), .Q(s[29]));  // open: Qn, preset, reset
  D_Flip_Flop d_ff_31 (.D(multiplexer_31_out), .clk(CLK), .Q(s[30]));  // open: Qn, preset, reset
  D_Flip_Flop d_ff_32 (.D(multiplexer_32_out), .clk(CLK), .Q(s[31]));  // open: Qn, preset, reset
endmodule

module Banco_de_registradores (
  input  [31:0] in_1,
  input  [3:0] in_2
);

  wire demultiplexer_2_out1, demultiplexer_2_out2, demultiplexer_2_out3, demultiplexer_2_out4,
       demultiplexer_2_out5, demultiplexer_2_out6, demultiplexer_2_out7, demultiplexer_2_out8,
       demultiplexer_2_out9, demultiplexer_2_out10, demultiplexer_2_out11, demultiplexer_2_out12,
       demultiplexer_2_out13, demultiplexer_2_out14, demultiplexer_2_out15;
  wire [3:0] undriven;
  wire [31:0] demultiplexer_1_out0, demultiplexer_1_out1, demultiplexer_1_out2, demultiplexer_1_out3,
       demultiplexer_1_out4, demultiplexer_1_out5, demultiplexer_1_out6, demultiplexer_1_out7,
       demultiplexer_1_out8, demultiplexer_1_out9, demultiplexer_1_out10, demultiplexer_1_out11,
       demultiplexer_1_out12, demultiplexer_1_out13, demultiplexer_1_out14, demultiplexer_1_out15,
       registrador_1_s, registrador_2_s, registrador_3_s, registrador_4_s, registrador_5_s, registrador_6_s,
       registrador_7_s, registrador_8_s, registrador_9_s, registrador_10_s, registrador_11_s,
       registrador_12_s, registrador_13_s, registrador_14_s, registrador_15_s, registrador_16_s;

  Demultiplexer #(.select(4), .width(32)) demultiplexer_1 (
    .out0(demultiplexer_1_out0), .out1(demultiplexer_1_out1), .out2(demultiplexer_1_out2),
    .out3(demultiplexer_1_out3), .out4(demultiplexer_1_out4), .out5(demultiplexer_1_out5),
    .out6(demultiplexer_1_out6), .out7(demultiplexer_1_out7), .out8(demultiplexer_1_out8),
    .out9(demultiplexer_1_out9), .out10(demultiplexer_1_out10), .out11(demultiplexer_1_out11),
    .out12(demultiplexer_1_out12), .out13(demultiplexer_1_out13), .out14(demultiplexer_1_out14),
    .out15(demultiplexer_1_out15), .in(in_1), .sel(undriven));
  Demultiplexer #(.select(4)) demultiplexer_2 (
    .out1(demultiplexer_2_out1), .out2(demultiplexer_2_out2), .out3(demultiplexer_2_out3),
    .out4(demultiplexer_2_out4), .out5(demultiplexer_2_out5), .out6(demultiplexer_2_out6),
    .out7(demultiplexer_2_out7), .out8(demultiplexer_2_out8), .out9(demultiplexer_2_out9),
    .out10(demultiplexer_2_out10), .out11(demultiplexer_2_out11), .out12(demultiplexer_2_out12),
    .out13(demultiplexer_2_out13), .out14(demultiplexer_2_out14), .out15(demultiplexer_2_out15));  // open: out0, in, sel
  Registrador registrador_1 (.a(demultiplexer_1_out0), .W_En(demultiplexer_2_out1), .s(registrador_1_s));  // open: CLK
  Registrador registrador_2 (.a(demultiplexer_1_out1), .W_En(demultiplexer_2_out2), .s(registrador_2_s));  // open: CLK
  Registrador registrador_3 (.a(demultiplexer_1_out2), .W_En(demultiplexer_2_out3), .s(registrador_3_s));  // open: CLK
  Registrador registrador_4 (.a(demultiplexer_1_out3), .W_En(demultiplexer_2_out4), .s(registrador_4_s));  // open: CLK
  Registrador registrador_5 (.a(demultiplexer_1_out4), .W_En(demultiplexer_2_out5), .s(registrador_5_s));  // open: CLK
  Registrador registrador_6 (.a(demultiplexer_1_out5), .W_En(demultiplexer_2_out6), .s(registrador_6_s));  // open: CLK
  Registrador registrador_7 (.a(demultiplexer_1_out6), .W_En(demultiplexer_2_out7), .s(registrador_7_s));  // open: CLK
  Registrador registrador_8 (.a(demultiplexer_1_out7), .W_En(demultiplexer_2_out8), .s(registrador_8_s));  // open: CLK
  Registrador registrador_9 (.a(demultiplexer_1_out8), .W_En(demultiplexer_2_out9), .s(registrador_9_s));  // open: CLK
  Registrador registrador_10 (
    .a(demultiplexer_1_out9), .W_En(demultiplexer_2_out10), .s(registrador_10_s));  // open: CLK
  Registrador registrador_11 (
    .a(demultiplexer_1_out10), .W_En(demultiplexer_2_out11), .s(registrador_11_s));  // open: CLK
  Registrador registrador_12 (.a(demultiplexer_1_out11), .s(registrador_12_s));  // open: W_En, CLK
  Registrador registrador_13 (
    .a(demultiplexer_1_out12), .W_En(demultiplexer_2_out12), .s(registrador_13_s));  // open: CLK
  Registrador registrador_14 (
    .a(demultiplexer_1_out13), .W_En(demultiplexer_2_out13), .s(registrador_14_s));  // open: CLK
  Registrador registrador_15 (
    .a(demultiplexer_1_out14), .W_En(demultiplexer_2_out14), .s(registrador_15_s));  // open: CLK
  Registrador registrador_16 (
    .a(demultiplexer_1_out15), .W_En(demultiplexer_2_out15), .s(registrador_16_s));  // open: CLK
  Multiplexer #(.select(4), .width(32)) multiplexer_1 (
    .in0(registrador_1_s), .in1(registrador_2_s), .in2(registrador_3_s), .in3(registrador_4_s),
    .in4(registrador_5_s), .in5(registrador_6_s), .in6(registrador_7_s), .in7(registrador_8_s),
    .in8(registrador_9_s), .in9(registrador_10_s), .in10(registrador_11_s), .in11(registrador_12_s),
    .in12(registrador_13_s), .in13(registrador_14_s), .in14(registrador_15_s), .in15(registrador_16_s),
    .sel(in_2));  // open: out
endmodule
